# Fritzing sketch MQTT Sensor (saved by Fritzing 0.9.3b)
breadboards: 1

parts:
  DHT1 = DHT22 Humidity and Temperature Sensor
  Raspberry_Pi_1 = Raspberry Pi 3 [part_number=RPI-3-V1.2]
  Part1 = OLED Monochrome 128x64 1.3 inch [part_number=938]
  R1 = Resistor [tolerance=±5% resistance=10k package=THT]

nets:
  VDD: DHT1.VDD, Raspberry_Pi_1.3v3, Part1.3.3V, R1.Pin_1
  N1: DHT1.DATA, Raspberry_Pi_1.GIPO4, R1.Pin_0
  GND: DHT1.GND, Raspberry_Pi_1.GND, Part1.GND
  N2: Raspberry_Pi_1.GPIO2, Part1.MOSI_SDA
  N3: Raspberry_Pi_1.GPIO3, Part1.SCLK_SCK

custom parts:
  OLED Monochrome 128x64 1.3 inch: These displays are small, only about 1.3" diagonal, but very readable due to the high contrast of an OLED display. This display is made of 128x64 individual white OLED pixels, each one is turned on or off by the controller chip. Because the display makes its own light, no backlight is required. This reduces the power required to run the OLED and is why the display has such high contrast; we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
